// Logisim project MUXX.circ as structural Verilog: 2 circuits, main circuit main
module main (
  input  S0,
  input  S1,
  input  Io,
  input  I1,
  input  I2,
  input  I3,
  output out_7
);

  wire and_1_out, and_2_out, and_3_out, and_4_out, not_1_out, not_2_out;

  not not_1 (not_1_out, S0);
  not not_2 (not_2_out, S1);
  and and_1 (and_1_out, Io, not_1_out, not_2_out);
  and and_2 (and_2_out, I1, S0, not_2_out);
  and and_3 (and_3_out, I2, not_1_out, S1);
  and and_4 (and_4_out, I3, S0, S1);
  or or_1 (out_7, and_1_out, and_2_out, and_3_out, and_4_out);
endmodule

module MUX (
  input  in_1,
  input  in_2,
  input  in_3,
  input  in_4,
  input  in_5,
  input  in_6
);

  wire main_1_out_7;

  main main_1 (.S0(in_1), .S1(in_2), .Io(in_3), .I1(in_4), .I2(in_5), .I3(in_6), .out_7(main_1_out_7));
  LED led_1 (.in(main_1_out_7));
endmodule
