// Logisim project decoderr.circ as structural Verilog
module Decoder (
  input  x,
  input  y,
  input  z,
  output [7:0] D
);

  wire not_1_out, not_2_out, not_3_out;

  not not_1 (not_1_out, x);
  not not_2 (not_2_out, y);
  not not_3 (not_3_out, z);
  and and_1 (D[7], not_1_out, not_2_out, not_3_out);
  and and_2 (D[6], not_1_out, not_2_out, z);
  and and_3 (D[5], not_1_out, y, not_3_out);
  and and_4 (D[4], not_1_out, y, z);
  and and_5 (D[3], x, not_2_out, not_3_out);
  and and_6 (D[2], x, not_2_out, z);
  and and_7 (D[1], x, y, not_3_out);
  and and_8 (D[0], x, y, z);

  // Notes on the sheet:
  //   d0,d1,d2,d3,d4,d5,d6,d7
endmodule
