// Logisim project savensegment.circ as structural Verilog
module \final  (
  input  A,
  input  in_2,
  input  C,
  input  D,
  output out_5,
  output b,
  output out_7,
  output out_8,
  output e,
  output f,
  output g
);

  wire and_1_out, and_2_out, and_3_out, and_4_out, and_5_out, and_6_out, and_7_out, and_8_out, and_9_out,
       and_10_out, and_11_out, and_12_out, and_13_out, and_14_out, and_15_out, and_16_out, not_1_out,
       not_2_out, not_3_out;

  not not_1 (not_1_out, in_2);
  not not_2 (not_2_out, C);
  not not_3 (not_3_out, D);
  and and_1 (and_1_out, not_1_out, not_3_out);
  and and_2 (and_2_out, in_2, D);
  and and_3 (and_3_out, not_2_out, not_3_out);
  and and_4 (and_4_out, C, D);
  or or_1 (out_7, not_2_out, D, in_2);
  and and_5 (and_5_out, not_1_out, not_3_out);
  and and_6 (and_6_out, not_1_out, C);
  and and_7 (and_7_out, in_2, not_2_out, D);
  and and_8 (and_8_out, C, not_3_out);
  and and_9 (and_9_out, not_1_out, not_3_out);
  and and_10 (and_10_out, C, not_3_out);
  and and_11 (and_11_out, not_2_out, not_3_out);
  and and_12 (and_12_out, in_2, not_2_out);
  and and_13 (and_13_out, in_2, not_3_out);
  and and_14 (and_14_out, not_1_out, C);
  and and_15 (and_15_out, in_2, not_2_out);
  and and_16 (and_16_out, C, not_3_out);
  or or_2 (out_5, and_1_out, C, and_2_out, A);
  or or_3 (b, not_1_out, and_3_out, and_4_out);
  or or_4 (out_8, and_5_out, and_6_out, and_7_out, and_8_out, A);
  or or_5 (e, and_9_out, and_10_out);
  or or_6 (f, and_11_out, and_12_out, and_13_out, A);
  or or_7 (g, and_14_out, and_15_out, A, and_16_out);
  _7_Segment_Display u_7_segment_display_1 (.g(g), .f(f), .a(out_5), .b(b), .e(e), .d(out_8), .c(out_7));  // open: dp
endmodule
