// Logisim project 4bitEVENparity.circ as structural Verilog: 1 circuit, main circuit main
module main (
  input  A,
  input  B,
  input  C,
  input  P,
  output out_5
);

  wire xor_1_out, xor_2_out;

  xor xor_1 (xor_1_out, A, B);
  xor xor_2 (xor_2_out, C, P);
  xor xor_3 (out_5, xor_1_out, xor_2_out);

  // Notes on the sheet:
  //   Equation = A EXOR B EXOR C EXOR D
endmodule
