// Logisim project 4bitcomparator.circ as structural Verilog: 1 circuit, main circuit main
module main (
  input  [3:0] A,
  input  [3:0] B
);

  wire comparator_1_eq, comparator_1_gt, comparator_1_lt;

  Comparator #(.mode("unsigned"), .width(4)) comparator_1 (
    .a(A), .b(B), .gt(comparator_1_gt), .eq(comparator_1_eq), .lt(comparator_1_lt));
  DotMatrix #(.matrixcols(3), .matrixrows(1)) dotmatrix_1 (
    .col0(comparator_1_gt), .col1(comparator_1_eq), .col2(comparator_1_lt));
endmodule
