// Logisim project BCDtoEXCESS3.circ as structural Verilog: 1 circuit, main circuit main
module main (
  input  A,
  input  B,
  input  C,
  input  D,
  output W,
  output X,
  output Y,
  output Z
);

  wire and_1_out, and_2_out;

  and and_1 (and_1_out, B, C);
  and and_2 (and_2_out, B, D);
  xnor xnor_1 (Y, C, D);
  not not_1 (Z, D);
  ExactlyOne xor_1 (.out(X), .in0(B), .in1(C), .in2(D));
  or or_1 (W, A, and_1_out, and_2_out);
endmodule
