// Logisim project Hexa_To_Binary.circ as structural Verilog: 1 circuit, main circuit main
module main (
  input  _0,
  input  _1,
  input  _2,
  input  _3,
  input  _4,
  input  _5,
  input  _6,
  input  _7,
  input  _8,
  input  _9,
  input  A,
  input  B,
  input  C,
  input  D,
  input  E,
  input  F,
  output B0,
  output B1,
  output B2,
  output B3
);

  or or_1 (B0, _1, _3, _5, _7, _9, B, D, F);
  or or_2 (B1, _2, _3, _6, _7, A, B, E, F);
  or or_3 (B2, _4, _5, _6, _7, C, D, E, F);
  or or_4 (B3, _8, _9, A, B, C, D, E, F);

  // Notes on the sheet:
  //   B0=1+3+5+7+9+B+D+F
  //   B1=2+3+6+7+A+B+E+F
  //   B2=4+5+6+7+C+D+E+F
  //   B3=8+9+A+B+C+D+E+F
  //   Hexadecimal to binary 16*4
endmodule
