// Logisim project Mux.circ as structural Verilog: 1 circuit, main circuit main
module main (
  input  in_1,
  input  in_2,
  input  in_3,
  input  in_4,
  input  [1:0] in_5,
  input  in_6
);

  wire multiplexer_1_out;

  Multiplexer #(.enable("true"), .select(2)) multiplexer_1 (
    .in0(in_1), .in1(in_2), .in2(in_4), .in3(in_3), .out(multiplexer_1_out), .sel(in_5), .en(in_6));
  LED led_1 (.in(multiplexer_1_out));

  // Notes on the sheet:
  //   ar select/enable line 2 bit kore dite hbe 
  //   eta 1 mane bujhay MUX on
endmodule
