// Logisim project Tflipflop.circ as structural Verilog: 2 circuits, main circuit main
module main (
  input  in_1,
  input  J,
  input  in_3
);

  wire clock_1_out, clock_2_out, nand_1_out, nand_2_out, nand_3_out, nand_4_out, t_ff_1_q, t_ff_1_qn;

  Clock clock_1 (.out(clock_1_out));
  nand nand_1 (nand_1_out, nand_4_out, J, clock_1_out);
  nand nand_2 (nand_2_out, clock_1_out, J, nand_3_out);
  T_Flip_Flop t_ff_1 (.T(in_1), .clk(clock_2_out), .Q(t_ff_1_q), .Qn(t_ff_1_qn));  // open: reset, preset
  Clock clock_2 (.out(clock_2_out));
  LED led_1 (.in(t_ff_1_qn));
  LED led_2 (.in(t_ff_1_q));
  nand nand_3 (nand_3_out, nand_1_out, nand_4_out);
  nand nand_4 (nand_4_out, nand_3_out, nand_2_out);
  LED led_3 (.in(nand_3_out));
  LED led_4 (.in(nand_4_out));

  // Notes on the sheet:
  //   K
endmodule

module jkflip (
  input  in_1,
  input  in_2
);

  wire undriven;

  main main_1 (.in_1(in_1), .J(in_2));  // open: in_3
  Clock clock_1 ();  // open: out
  LED led_1 (.in(undriven));
endmodule
