// Logisim project cubeee.circ as structural Verilog: 1 circuit, main circuit main
module main (
  input  A,
  input  B,
  input  in_3,
  output Yo,
  output y1,
  output y2,
  output y3,
  output out_8
);

  wire not_1_out, not_2_out;

  not not_1 (not_1_out, A);
  not not_2 (not_2_out, B);
  and and_1 (y1, A, B);
  and and_2 (out_8, A, B);

  assign y2 = in_3;
  assign y3 = A;
  assign Yo = B;

  // Notes on the sheet:
  //   y4
endmodule
