// Logisim project EvenParityBItchecker.circ as structural Verilog: 2 circuits, main circuit main
module main (
  input  in_1,
  input  in_2,
  input  in_3,
  output out_4,
  output out_5
);

  wire xor_1_out;

  xor xor_1 (xor_1_out, in_1, in_2);
  xor xor_2 (out_4, xor_1_out, in_3);
  Even even_1 (.in_1(in_1), .in_2(in_2), .in_3(in_3), .out_4(out_5));

  // Notes on the sheet:
  //   3 Bit Even parity Bit Checker
endmodule

module Even (
  input  in_1,
  input  in_2,
  input  in_3,
  output out_4
);

  wire xor_1_out;

  xor xor_1 (xor_1_out, in_1, in_2);
  xor xor_2 (out_4, xor_1_out, in_3);
endmodule
