// Logisim project FullSubtractor.circ as structural Verilog: 1 circuit, main circuit main
module main (
  input  in_1,
  input  in_2,
  input  in_3,
  output out_4,
  output out_5
);

  wire and_1_out, and_2_out, n7404_1_pin2, n7404_1_pin4, n7408_1_pin3, n7408_1_pin6, n7486_1_pin3, not_1_out,
       not_2_out, or_1_out, xor_1_out, xor_2_out;

  _7486 u_7486_1 (
    .pin1(in_1), .pin2(in_2), .pin3(n7486_1_pin3), .pin4(n7486_1_pin3), .pin5(in_3), .pin6(out_5));  // open: pin13, pin12, pin11, pin10, pin9, pin8
  xor xor_1 (xor_1_out, in_1, in_2);
  not not_1 (not_1_out, in_1);
  and and_1 (and_1_out, not_1_out, in_2);
  _7404 u_7404_1 (
    .pin1(in_1), .pin2(n7404_1_pin2), .pin3(n7486_1_pin3), .pin4(n7404_1_pin4));  // open: pin5, pin6, pin13, pin12, pin11, pin10, pin9, pin8
  xor xor_2 (xor_2_out, xor_1_out, in_3);
  not not_2 (not_2_out, xor_1_out);
  and and_2 (and_2_out, not_2_out, in_3);
  _7408 u_7408_1 (
    .pin1(n7404_1_pin2), .pin2(in_2), .pin3(n7408_1_pin3), .pin4(n7404_1_pin4), .pin5(in_3),
    .pin6(n7408_1_pin6));  // open: pin13, pin12, pin11, pin10, pin9, pin8
  or or_1 (or_1_out, and_2_out, and_1_out);
  // _7432 7432_1: pin names not known; wires that end beside it: 1'b1, n7408_1_pin3, n7408_1_pin6, out_4, n7486_1_pin3
  LED led_1 (.in(xor_2_out));
  LED led_2 (.in(or_1_out));
  // also tied to GND on the sheet: n7486_1_pin3

  // Notes on the sheet:
  //   X-OR
  //   NOT
  //   AND
endmodule
