// Logisim project HalfSubtractor.circ as structural Verilog: 1 circuit, main circuit main
module main (
  input  in_1,
  input  in_2,
  output out_3,
  output out_4
);

  wire and_1_out, n7404_1_p3, not_1_out, xor_1_out;

  // _7486 7486_1: pin names not known; wires that end beside it: 1'b1, in_1, in_2, out_4, 1'b0
  xor xor_1 (xor_1_out, in_1, in_2);
  not not_1 (not_1_out, in_1);
  and and_1 (and_1_out, not_1_out, in_2);
  // _7404 7404_1: pin names not known; wires that end beside it: 1'b1, in_1, n7404_1_p3, 1'b0
  LED led_1 (.in(xor_1_out));
  LED led_2 (.in(and_1_out));
  // _7408 7408_1: pin names not known; wires that end beside it: 1'b1, n7404_1_p3, in_2, out_3, 1'b0

  // Notes on the sheet:
  //   X-OR
  //   NOT
  //   Diff..
  //   borrow
  //   AND
endmodule
