// Logisim project NORimplementation.circ as structural Verilog: 1 circuit, main circuit main
module main (
  input  C,
  input  D,
  input  B,
  input  A,
  output out_5
);

  wire and_1_out, and_2_out, and_3_out, nor_1_out, nor_2_out, nor_3_out, nor_4_out, nor_5_out, nor_6_out,
       nor_7_out, nor_8_out, nor_9_out, nor_10_out, nor_11_out, nor_12_out, nor_13_out, nor_14_out,
       nor_15_out, nor_16_out, nor_17_out, nor_18_out, nor_19_out, nor_20_out, nor_21_out, nor_22_out,
       nor_23_out, nor_24_out, not_1_out, not_2_out, not_3_out, or_1_out, undriven, undriven_2, undriven_3,
       undriven_4, undriven_5, undriven_6, undriven_7, undriven_8, undriven_9, undriven_10, undriven_11,
       undriven_12;

  not not_1 (not_1_out, undriven_5);
  not not_2 (not_2_out, undriven_2);
  not not_3 (not_3_out, C);
  nor nor_1 (nor_1_out, undriven_3, undriven_3);
  nor nor_2 (nor_2_out, undriven_4, undriven_4);
  nor nor_3 (nor_3_out, undriven_6, undriven_6);
  nor nor_4 (nor_4_out, not_1_out, not_1_out);
  nor nor_5 (nor_5_out, undriven_9, undriven_9);
  nor nor_6 (nor_6_out, undriven_10, undriven_10);
  nor nor_7 (nor_7_out, undriven, undriven);
  nor nor_8 (nor_8_out, not_2_out, not_2_out);
  and and_1 (and_1_out, C, D);
  and and_2 (and_2_out, B, not_3_out);
  nor nor_9 (nor_9_out, nor_1_out, nor_2_out);
  nor nor_10 (nor_10_out, nor_3_out, nor_4_out);
  nor nor_11 (nor_11_out, nor_5_out, nor_6_out);
  nor nor_12 (nor_12_out, nor_7_out, nor_8_out);
  or or_1 (or_1_out, and_1_out, B);
  nor nor_13 (nor_13_out, nor_9_out, undriven_7);
  nor nor_14 (nor_14_out, nor_11_out, undriven_11);
  and and_3 (and_3_out, or_1_out, A);
  nor nor_15 (nor_15_out, nor_13_out, nor_13_out);
  or or_2 (out_5, and_3_out, and_2_out);
  nor nor_16 (nor_16_out, nor_15_out, nor_15_out);
  nor nor_17 (nor_17_out, undriven_8, undriven_8);
  nor nor_18 (nor_18_out, undriven_12, undriven_12);
  nor nor_19 (nor_19_out, nor_16_out, nor_17_out);
  nor nor_20 (nor_20_out, nor_14_out, nor_18_out);
  nor nor_21 (nor_21_out, nor_19_out, nor_10_out);
  nor nor_22 (nor_22_out, nor_20_out, nor_12_out);
  nor nor_23 (nor_23_out, nor_21_out, nor_21_out);
  nor nor_24 (nor_24_out, nor_22_out, nor_22_out);

  // Notes on the sheet:
  //   C'
endmodule
