// Logisim project half.circ as structural Verilog: 1 circuit, main circuit main
module main (
  input  in_1,
  input  in_2
);

  wire and_1_out, n7408_1_p4, n7486_1_p4, xor_1_out;

  xor xor_1 (xor_1_out, in_1, in_2);
  and and_1 (and_1_out, in_2, in_1);
  // _7486 7486_1: pin names not known; wires that end beside it: 1'b1, in_1, in_2, n7486_1_p4, 1'b0
  LED led_1 ();  // open: in
  LED led_2 (.in(xor_1_out));
  LED led_3 (.in(and_1_out));
  // _7408 7408_1: pin names not known; wires that end beside it: 1'b1, in_2, in_1, n7408_1_p4, 1'b0
  LED led_4 ();  // open: in
endmodule
