// Logisim project lockaheadcarry.circ as structural Verilog: 2 circuits, main circuit main
module main (
  input  A3,
  input  A2,
  input  A1,
  input  A0,
  input  Cin,
  input  B3,
  input  B2,
  input  B1,
  input  B0,
  output out_10,
  output out_11,
  output out_12,
  output out_13,
  output out_14
);

  wire and_1_out, and_2_out, and_3_out, and_4_out, and_5_out, and_6_out, and_7_out, and_8_out, and_9_out,
       and_10_out, C0_out, C1_out, C2_out, G0_out, G1_out, G2_out, G3_out, P0_out, P1_out, P2_out, P3_out;

  and and_1 (and_1_out, P3_out, G2_out);
  and and_2 (and_2_out, P3_out, P2_out, G1_out);
  or or_1 (out_14, G3_out, and_1_out, and_2_out, and_3_out, and_4_out);
  xor P3 (P3_out, A3, B3);
  and and_3 (and_3_out, P3_out, P2_out, P1_out, G0_out);
  and G3 (G3_out, B3, A3);
  and and_4 (and_4_out, P3_out, P2_out, P1_out, P0_out, Cin);
  xor P2 (P2_out, A2, B2);
  and G2 (G2_out, B2, A2);
  and and_5 (and_5_out, P2_out, G1_out);
  and and_6 (and_6_out, P2_out, P1_out, G0_out);
  or C2 (C2_out, G2_out, and_5_out, and_6_out, and_7_out);
  xor xor_1 (out_10, P3_out, C2_out);
  and and_7 (and_7_out, P2_out, P1_out, P0_out, Cin);
  xor P1 (P1_out, A1, B1);
  and G1 (G1_out, B1, A1);
  xor P0 (P0_out, A0, B0);
  and and_8 (and_8_out, P1_out, G0_out);
  or C1 (C1_out, G1_out, and_8_out, and_9_out);
  xor xor_2 (out_11, P2_out, C1_out);
  and G0 (G0_out, B0, A0);
  and and_9 (and_9_out, P1_out, P0_out, Cin);
  and and_10 (and_10_out, P0_out, Cin);
  or C0 (C0_out, G0_out, and_10_out);
  xor xor_3 (out_12, P1_out, C0_out);
  xor xor_4 (out_13, P0_out, Cin);
endmodule

module lookahedcarry (
  input  A3,
  input  A2,
  input  A1,
  input  A0,
  input  Cin,
  input  B3,
  input  B2,
  input  B1,
  input  B0,
  input  in_10,
  input  in_11,
  input  in_12,
  input  in_13,
  input  in_14,
  input  in_15,
  input  in_16,
  output out_17,
  output out_18,
  output out_19,
  output out_20,
  output out_21,
  output out_22,
  output out_23,
  output out_24,
  output out_25,
  output out_26
);

  wire and_1_out, and_2_out, and_3_out, and_4_out, and_5_out, and_6_out, and_7_out, and_8_out, and_9_out,
       and_10_out, C0_out, C1_out, C2_out, G0_out, G1_out, G2_out, G3_out, P0_out, P1_out, P2_out, P3_out;

  and and_1 (and_1_out, P3_out, G2_out);
  and and_2 (and_2_out, P3_out, P2_out, G1_out);
  or or_1 (out_26, G3_out, and_1_out, and_2_out, and_3_out, and_4_out);
  xor P3 (P3_out, A3, B3);
  and and_3 (and_3_out, P3_out, P2_out, P1_out, G0_out);
  and G3 (G3_out, B3, A3);
  and and_4 (and_4_out, P3_out, P2_out, P1_out, P0_out, Cin);
  xor P2 (P2_out, A2, B2);
  and G2 (G2_out, B2, A2);
  and and_5 (and_5_out, P2_out, G1_out);
  and and_6 (and_6_out, P2_out, P1_out, G0_out);
  or C2 (C2_out, G2_out, and_5_out, and_6_out, and_7_out);
  xor xor_1 (out_22, P3_out, C2_out);
  and and_7 (and_7_out, P2_out, P1_out, P0_out, Cin);
  xor P1 (P1_out, A1, B1);
  and G1 (G1_out, B1, A1);
  xor P0 (P0_out, A0, B0);
  and and_8 (and_8_out, P1_out, G0_out);
  or C1 (C1_out, G1_out, and_8_out, and_9_out);
  xor xor_2 (out_23, P2_out, C1_out);
  and G0 (G0_out, B0, A0);
  and and_9 (and_9_out, P1_out, P0_out, Cin);
  and and_10 (and_10_out, P0_out, Cin);
  or C0 (C0_out, G0_out, and_10_out);
  xor xor_3 (out_24, P1_out, C0_out);
  xor xor_4 (out_25, P0_out, Cin);
  main main_1 (
    .A3(in_10), .A2(in_11), .A1(in_12), .Cin(in_13), .B3(in_14), .B2(in_15), .B1(in_16), .out_10(out_17),
    .out_11(out_18), .out_12(out_19), .out_13(out_20), .out_14(out_21));  // open: A0, B0
endmodule
