// Logisim project xm.circ as structural Verilog: 2 circuits, main circuit main
module main (
  input  W_prime,
  input  x_prime,
  input  y,
  input  w_prime_2,
  input  x,
  input  z,
  input  x_2,
  input  y_prime,
  input  z_2,
  input  w,
  input  y_2,
  input  z_prime,
  output F
);

  wire nand_1_out, nand_2_out, nand_3_out, nand_4_out, nand_5_out, nand_6_out, nand_7_out, nand_8_out,
       nand_9_out, nand_10_out, nand_11_out, nand_12_out, nand_13_out, nand_14_out, nand_15_out, nand_16_out;

  nand nand_1 (nand_1_out, w, y_2);
  nand nand_2 (nand_2_out, W_prime, x_prime);
  nand nand_3 (nand_3_out, w_prime_2, x);
  nand nand_4 (nand_4_out, x_2, y_prime);
  nand nand_5 (nand_5_out, nand_2_out, nand_2_out);
  nand nand_6 (nand_6_out, nand_3_out, nand_3_out);
  nand nand_7 (nand_7_out, nand_4_out, nand_4_out);
  nand nand_8 (nand_8_out, nand_1_out, nand_1_out);
  nand nand_9 (nand_9_out, nand_8_out, z_prime);
  nand nand_10 (nand_10_out, nand_5_out, y);
  nand nand_11 (nand_11_out, nand_6_out, z);
  nand nand_12 (nand_12_out, nand_7_out, z_2);
  nand nand_13 (nand_13_out, nand_10_out, nand_11_out);
  nand nand_14 (nand_14_out, nand_12_out, nand_9_out);
  nand nand_15 (nand_15_out, nand_13_out, nand_13_out);
  nand nand_16 (nand_16_out, nand_14_out, nand_14_out);
  nand nand_17 (F, nand_15_out, nand_16_out);
endmodule

module combi (
  input  W_prime,
  input  x_prime,
  input  y,
  input  w_prime_2,
  input  x,
  input  z,
  input  x_2,
  input  y_prime,
  input  z_2,
  input  w,
  input  y_2,
  input  z_prime,
  input  in_13,
  input  in_14,
  input  in_15,
  input  in_16,
  input  in_17,
  input  in_18,
  input  in_19,
  input  in_20,
  input  in_21,
  input  in_22,
  input  in_23,
  input  in_24,
  output F
);

  wire main_1_f, nand_1_out, nand_2_out, nand_3_out, nand_4_out, nand_5_out, nand_6_out, nand_7_out,
       nand_8_out, nand_9_out, nand_10_out, nand_11_out, nand_12_out, nand_13_out, nand_14_out, nand_15_out,
       nand_16_out;

  nand nand_1 (nand_1_out, w, y_2);
  nand nand_2 (nand_2_out, W_prime, x_prime);
  nand nand_3 (nand_3_out, w_prime_2, x);
  nand nand_4 (nand_4_out, x_2, y_prime);
  nand nand_5 (nand_5_out, nand_2_out, nand_2_out);
  nand nand_6 (nand_6_out, nand_3_out, nand_3_out);
  nand nand_7 (nand_7_out, nand_4_out, nand_4_out);
  nand nand_8 (nand_8_out, nand_1_out, nand_1_out);
  nand nand_9 (nand_9_out, nand_8_out, z_prime);
  nand nand_10 (nand_10_out, nand_5_out, y);
  nand nand_11 (nand_11_out, nand_6_out, z);
  nand nand_12 (nand_12_out, nand_7_out, z_2);
  nand nand_13 (nand_13_out, nand_10_out, nand_11_out);
  nand nand_14 (nand_14_out, nand_12_out, nand_9_out);
  main main_1 (
    .W_prime(in_13), .x_prime(in_14), .y(in_15), .w_prime_2(in_16), .x(in_17), .z(in_18), .x_2(in_19),
    .y_prime(in_20), .z_2(in_21), .w(in_22), .y_2(in_23), .z_prime(in_24), .F(main_1_f));
  LED led_1 (.in(main_1_f));
  nand nand_15 (nand_15_out, nand_13_out, nand_13_out);
  nand nand_16 (nand_16_out, nand_14_out, nand_14_out);
  nand nand_17 (F, nand_15_out, nand_16_out);
endmodule
